// Logisim project TD4.circ as structural Verilog: 1 circuit, main circuit main
module main (
  input  _3,
  input  _2,
  input  _1,
  input  _0
);

  wire adder_1_cout, button_1_out, clock_1_out, n7432_1_p1, n7432_1_p3, n7432_1_p10, n74153_1_p8,
       n74161_1_p7, n74161_1_p8, n74161_1_p9, n74161_1_p10, n74161_2_p9, n74161_2_p10, n74161_2_p11,
       n74161_2_p12, n74161_2_p13, n74161_3_p9, n74161_3_p10, n74161_3_p11, n74161_3_p12, n74161_3_p13,
       n74161_4_p10, n74161_4_p16, not_1_out, not_2_out;
  wire [3:0] n74153_2_p1, n74161_1_p3, n74161_4_p11;
  wire [7:0] rom_2_data;

  Clock clock_1 (.out(clock_1_out));
  Button button_1 (.out(button_1_out));
  not not_1 (not_1_out, button_1_out);
  // _74161 74161_1: pin names not known; wires that end beside it: not_1_out, clock_1_out, n74161_1_p3[0], n74161_1_p3[1], n74161_1_p3[2], n74161_1_p3[3], n74161_1_p7, n74161_1_p8, n74161_1_p9, n74161_1_p10
  // _74161 74161_2: pin names not known; wires that end beside it: 1'b0, not_1_out, clock_1_out, n74161_1_p3[0], n74161_1_p3[1], n74161_1_p3[2], n74161_1_p3[3], 1'b0, n74161_2_p9, n74161_2_p10, n74161_2_p11, n74161_2_p12, n74161_2_p13
  // _74161 74161_3: pin names not known; wires that end beside it: 1'b0, not_1_out, clock_1_out, n74161_1_p3[0], n74161_1_p3[1], n74161_1_p3[2], n74161_1_p3[3], 1'b0, n74161_3_p9, n74161_3_p10, n74161_3_p11, n74161_3_p12, n74161_3_p13
  // _74161 74161_4: pin names not known; wires that end beside it: 1'b0, not_1_out, clock_1_out, n74161_1_p3[0], n74161_1_p3[1], n74161_1_p3[2], n74161_1_p3[3], 1'b1, 1'b0, n74161_4_p10, n74161_4_p11[0], n74161_4_p11[1], n74161_4_p11[2], n74161_4_p11[3], 1'b1, n74161_4_p16
  LED led_1 (.in(n74161_3_p13));
  LED led_2 (.in(n74161_3_p12));
  LED led_3 (.in(n74161_3_p10));
  LED led_4 (.in(n74161_3_p11));
  // _74153 74153_1: pin names not known; wires that end beside it: 1'b0, rom_2_data[5], 1'b0, _0, n74161_2_p10, n74161_1_p7, 1'b0, n74153_1_p8, 1'b0, _1, n74161_2_p11
  // _74153 74153_2: pin names not known; wires that end beside it: n74153_2_p1[0], 1'b0, rom_2_data[5], 1'b0, _2, n74161_2_p12, n74161_1_p9, n74153_2_p1[2], n74161_1_p8, n74153_2_p1[1], 1'b0, n74153_1_p8, 1'b0, _3, n74161_2_p13, n74161_1_p10, n74153_2_p1[3]
  ROM #(.addrWidth(4)) rom_1 ();  // open: addr, data, sel
  ROM #(.addrWidth(4)) rom_2 (.addr(n74161_4_p11), .data(rom_2_data));  // open: sel
  Adder #(.width(4)) adder_1 (.a(n74153_2_p1), .b(rom_2_data[3:0]), .out(n74161_1_p3), .cin(1'b0), .cout(adder_1_cout));
  // _7432 7432_1: pin names not known; wires that end beside it: n7432_1_p1, rom_2_data[4], n7432_1_p3, rom_2_data[4], rom_2_data[7], n74153_1_p8, rom_2_data[6], rom_2_data[7], n74161_2_p9, n7432_1_p10, rom_2_data[7], n74161_3_p9
  not not_2 (not_2_out, not_1_out);
  // _7474 7474_1: pin names not known; wires that end beside it: not_2_out, adder_1_cout, clock_1_out, 1'b0, n7432_1_p1, 1'b0, 1'b0, 1'b0, 1'b0
  // _7410 7410_1: pin names not known; wires that end beside it: 1'b1, n7432_1_p10, 1'b1, 1'b1, rom_2_data[6], n7432_1_p10, rom_2_data[7], n74161_4_p10, rom_2_data[7], rom_2_data[6], n7432_1_p3, n74161_4_p16

  // Notes on the sheet:
  //   A reg
  //   B reg
  //   Output
  //   PC
  //   0
  //   1
  //   2
  //   3
  //   MPX
  //   SELECT A
  //   SELECT B
  //   contents of rom_1 (hex, n*v repeats v):
  //   b3 b6 bc b8 b8 bc b6 b3 b1 f0
  //   contents of rom_2 (hex, n*v repeats v):
  //   b7 1 e1 1 e3 b6 1 e6 1 e8 b0 b4 1 ea b8 ff
  //   !LOAD 0, 1, 2, 3
  //   immediate data
  //   operation code
endmodule
